# Fritzing sketch Untitled Sketch (saved by Fritzing 0.9.3b)
breadboards: 3

parts:
  부품1 = Arduino Mega 2560 (Rev3)
  R1 = Resistor [tolerance=±5% resistance=220 package=THT]
  R2 = Resistor [tolerance=±5% resistance=220 package=THT]
  R3 = Resistor [tolerance=±5% resistance=220 package=THT]
  R4 = Resistor [tolerance=±5% resistance=220 package=THT]
  R5 = Resistor [tolerance=±5% resistance=220 package=THT]
  R6 = Resistor [tolerance=±5% resistance=220 package=THT]
  R7 = Resistor [tolerance=±5% resistance=220 package=THT]
  R8 = Resistor [tolerance=±5% resistance=220 package=THT]
  R9 = Resistor [tolerance=±5% resistance=220 package=THT]
  R10 = Resistor [tolerance=±5% resistance=220 package=THT]
  R11 = Resistor [tolerance=±5% resistance=220 package=THT]
  R12 = Resistor [tolerance=±5% resistance=220 package=THT]
  LED1 = LED - 5mm [color="Red (633nm)" package="5 mm [THT]"]
  LED2 = LED - 5mm [color="Red (633nm)" package="5 mm [THT]"]
  LED3 = LED - 5mm [color="Red (633nm)" package="5 mm [THT]"]
  LED4 = LED - 5mm [color="Red (633nm)" package="5 mm [THT]"]
  LED5 = LED - 5mm [color="Yellow (595nm)" package="5 mm [THT]"]
  LED7 = LED - 5mm [color="Yellow (595nm)" package="5 mm [THT]"]
  LED8 = LED - 5mm [color="Yellow (595nm)" package="5 mm [THT]"]
  LED9 = LED - 5mm [color="Yellow (595nm)" package="5 mm [THT]"]
  LED10 = LED - 5mm [color="Green (570nm)" package="5 mm [THT]"]
  LED11 = LED - 5mm [color="Green (570nm)" package="5 mm [THT]"]
  LED12 = LED - 5mm [color="Green (570nm)" package="5 mm [THT]"]
  LED13 = LED - 5mm [color="Green (570nm)" package="5 mm [THT]"]
  S1 = Pushbutton [package="[THT]"]
  S2 = Pushbutton [package="[THT]"]

nets:
  N1: 부품1.D12_PWM, R1.Pin_1
  N2: 부품1.D11_PWM, R2.Pin_1
  N3: 부품1.D10_PWM, R3.Pin_1
  N4: 부품1.GND, LED1.cathode, LED2.cathode, LED3.cathode, LED4.cathode, LED5.cathode, LED7.cathode, LED8.cathode, LED9.cathode, LED10.cathode, LED11.cathode, LED12.cathode, LED13.cathode, S1.Pin_3, S1.Pin_4, S2.Pin_3, S2.Pin_4
  N5: 부품1.D2_PWM, S1.Pin_1, S1.Pin_2
  N6: 부품1.D3_PWM, S2.Pin_1, S2.Pin_2
  N7: 부품1.D4_PWM, R4.Pin_1
  N8: 부품1.D5_PWM, R5.Pin_1
  N9: 부품1.D6_PWM, R6.Pin_1
  N10: 부품1.D26, R9.Pin_1
  N11: 부품1.D28, R8.Pin_1
  N12: 부품1.D30, R7.Pin_1
  N13: 부품1.D39, R10.Pin_1
  N14: 부품1.D41, R11.Pin_1
  N15: 부품1.D43, R12.Pin_1
  N16: R1.Pin_0, LED1.anode
  N17: R2.Pin_0, LED5.anode
  N18: R3.Pin_0, LED10.anode
  N19: R4.Pin_0, LED11.anode
  N20: R5.Pin_0, LED7.anode
  N21: R6.Pin_0, LED2.anode
  N22: R7.Pin_0, LED12.anode
  N23: R8.Pin_0, LED8.anode
  N24: R9.Pin_0, LED4.anode
  N25: R10.Pin_0, LED3.anode
  N26: R11.Pin_0, LED9.anode
  N27: R12.Pin_0, LED13.anode
